# Fritzing sketch ir_beam_led_stairs (saved by Fritzing 0.9.6b)

parts:
  Mod1 = Raspberry Pi Pico
  LED1 = RGB LED (com. cathode, rgb) [package="5 mm [THT]"]
  Power_plug1 = Power plug
  Power_plug2 = Power plug  # not connected
  U3 = G3VM-61E1 [package=g3vm-61e1]
  IR1 = TSOP312.., 314.. [package=THT]
  J1 = Camdenboss CTB0158-4 [part_number=CTB0158-4 package=THT]
  J2 = female pin header, 2 pins [form="♀ (female)"]
  U6 = Transformer [package=transformer]
  JP1 = Header 4 [package=jst-4-pth]
  JP2 = Header 2 [package=molex-1x2_lock]
  IR2 = TSOP312.., 314.. [package=THT]
  JP3 = Header 4 [package=screwterminal-3.5mm-4_lock]

nets:
  N1: Mod1.pin_3, Mod1.pin_28, Mod1.pin_42, U3.P$2, U3.P$6, JP3.4
  N2: Mod1.pin_24, IR1.Data
  N3: Mod1.pin_27, U3.P$3
  N4: Mod1.pin_40, U3.P$1
  N5: LED1.red_anode, JP3.1
  N6: LED1.common_cathode, JP3.2
  N7: LED1.green_anode, JP3.3
  N8: LED1.blue_anode, U3.P$4
  N9: Power_plug1.VCC, J2.pin1
  N10: Power_plug1.GND, J2.pin2
  N11: IR1.GND, JP1.2
  N12: IR1.Vs, JP1.1
  N13: J1.terminal_1, U6.2
  N14: J1.terminal_2, U6.1
  N15: J1.terminal_3, JP2.2
  N16: J1.terminal_4, JP2.1
  N17: JP1.3, IR2.Vs
  N18: JP1.4, IR2.GND

notes:
  5v usb pwr supply
  12v pwr supply
  step down to 5v
  IR beam break sensors
  RED is power [5v or 12v]
  BLACK is ground
  BLUE is beam break trigger
  YELOOW is relay H/L signal

custom parts:
  Raspberry Pi Pico: Raspberry Pi Pico. Based around the RP2040 microcontroller the Pico is a low cost microcontroller device bringing Raspberry Pi quality, cost, and easy of use to the microcontroller space. Jan 2021, Split part in to two versions: tht (this one) and SMD. This one will drill holes for a .1 in header in pcb to allow plugging in the module as well as providing pads to solder the module to the top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
